// Logisim project CPU_Final.circ as structural Verilog
module main (
  input  [4:0] in_1,
  input  in_2
);

  wire alu_1_zero, and_1_out, clock_1_out, exmem_1_zeroout, multiplexer_4_out, not_1_out, or_2_out;
  wire [1:0] control_unit_1_aluop, control_unit_1_alusrc, control_unit_1_regsrc, or_1_out;
  wire [2:0] exmem_1_wbout, idex_1_wbout, memwb_1_wbout;
  wire [2:2] control_unit_1_regwrite;
  wire [3:0] alu_control_1_control, idex_1_alucontrolout, idex_1_exout, ifid_1_instout_6;
  wire [4:0] exmem_1_mout, exmem_1_wbaddout, idex_1_wbaddout, ifid_1_instout_3, ifid_1_instout_4,
       ifid_1_instout_5, memwb_1_wbaddout;
  wire [5:0] control_unit_1_memread, idex_1_mout;
  wire [6:0] ifid_1_instout_2;
  wire [7:0] counter_1_q;
  wire [31:0] alu_1_result, exmem_1_aluout, exmem_1_pcout, exmem_1_pcpl4out, exmem_1_read2out,
       idex_1_immgenout, idex_1_pcout, idex_1_pcpl4out, idex_1_read1out, idex_1_read2out, ifid_1_pcout,
       ifid_1_pcpl4out, immgen_1_imm, memwb_1_aluout, memwb_1_pcpl4out, memwb_1_pcpliout, memwb_1_readout,
       multiplexer_1_out, multiplexer_2_out, multiplexer_3_out, multiplexer_5_out, pc2_1_pc_out, ram_1_dout,
       register_file_1_outa, register_file_1_outb, register_file_1_outregmanual, rom_1_data, somador_1_z,
       somador_2_z;
  wire [31:25] ifid_1_instout;

  Clock clock_1 (.out(clock_1_out));
  Counter counter_1 (.Q(counter_1_q), .clk(clock_1_out), .clr(in_2));  // open: load, D, count, carry, up
  PC2 pc2_1 (.clk(counter_1_q[0]), .reset(in_2), .pc_in(multiplexer_1_out), .pc_out(pc2_1_pc_out));
  ROM #(.addrWidth(24), .dataWidth(32)) rom_1 (.addr(pc2_1_pc_out[23:0]), .data(rom_1_data));
  somador somador_1 (.A(pc2_1_pc_out), .B(32'h1), .Z(somador_1_z));
  IFID ifid_1 (
    .clk(counter_1_q[0]), .pcIn(pc2_1_pc_out), .pcPl4In(somador_1_z), .instIn(rom_1_data),
    .pcOut(ifid_1_pcout), .pcPl4Out(ifid_1_pcpl4out),
    .instOut({ifid_1_instout[31], ifid_1_instout_6[3], ifid_1_instout[29:25], ifid_1_instout_4, ifid_1_instout_3, ifid_1_instout_6[2:0], ifid_1_instout_5, ifid_1_instout_2}));
  // Probe on {ifid_1_instout[31], ifid_1_instout_6[3], ifid_1_instout[29:25], ifid_1_instout_4, ifid_1_instout_3, ifid_1_instout_6[2:0], ifid_1_instout_5, ifid_1_instout_2}
  // Probe on register_file_1_outregmanual
  register_file register_file_1 (
    .\input (multiplexer_5_out), .regSelManual(in_1), .writeEnable(memwb_1_wbout[2]),
    .regASel(ifid_1_instout_3), .regBSel(ifid_1_instout_4), .writeRegSel(memwb_1_wbaddout),
    .clk(clock_1_out), .outA(register_file_1_outa), .outB(register_file_1_outb),
    .outRegManual(register_file_1_outregmanual));
  ImmGen immgen_1 (
    .inst({ifid_1_instout[31], ifid_1_instout_6[3], ifid_1_instout[29:25], ifid_1_instout_4, ifid_1_instout_3, ifid_1_instout_6[2:0], ifid_1_instout_5, ifid_1_instout_2}),
    .imm(immgen_1_imm));
  Control_Unit control_unit_1 (
    .opcode(ifid_1_instout_2), .AluSrc(control_unit_1_alusrc[0]), .blockA(control_unit_1_alusrc[1]),
    .RegWrite(control_unit_1_regwrite[2]), .MemRead(control_unit_1_memread[0]),
    .MemWrite(control_unit_1_memread[1]), .Branch(control_unit_1_memread[2]),
    .BranchNotEq(control_unit_1_memread[3]), .BrIncond(control_unit_1_memread[4]),
    .regToPC(control_unit_1_memread[5]), .AluOp(control_unit_1_aluop), .regSrc(control_unit_1_regsrc));
  Multiplexer #(.select(2), .width(32)) multiplexer_1 (
    .in0(somador_1_z), .in1(exmem_1_pcout), .in2(exmem_1_aluout), .in3(exmem_1_aluout),
    .out(multiplexer_1_out), .sel(or_1_out));
  // Probe on immgen_1_imm
  IDEX idex_1 (
    .clk(counter_1_q[0]), .pcIn(ifid_1_pcout), .read1In(register_file_1_outa),
    .read2In(register_file_1_outb), .immGenIn(immgen_1_imm), .aluControlin(ifid_1_instout_6),
    .wbAddIn(ifid_1_instout_5), .WBin({control_unit_1_regwrite[2], control_unit_1_regsrc}),
    .Min(control_unit_1_memread), .EXin({control_unit_1_aluop, control_unit_1_alusrc}),
    .pcPl4In(ifid_1_pcpl4out), .pcOut(idex_1_pcout), .read1Out(idex_1_read1out), .read2Out(idex_1_read2out),
    .immGenOut(idex_1_immgenout), .aluControlout(idex_1_alucontrolout), .wbAddOut(idex_1_wbaddout),
    .WBout(idex_1_wbout), .Mout(idex_1_mout), .EXout(idex_1_exout), .pcPl4Out(idex_1_pcpl4out));
  Multiplexer #(.width(32)) multiplexer_2 (
    .in0(idex_1_read1out), .in1({32{1'b0}}), .out(multiplexer_2_out), .sel(idex_1_exout[1]));
  Multiplexer #(.width(32)) multiplexer_3 (
    .in0(idex_1_read2out), .in1(idex_1_immgenout), .out(multiplexer_3_out), .sel(idex_1_exout[0]));
  somador somador_2 (.A(idex_1_pcout), .B(idex_1_immgenout), .Z(somador_2_z));
  ALU alu_1 (
    .A(multiplexer_2_out), .B(multiplexer_3_out), .control(alu_control_1_control), .result(alu_1_result),
    .zero(alu_1_zero));
  ALU_Control alu_control_1 (.Functs(idex_1_alucontrolout), .AluOp(idex_1_exout[3:2]), .Control(alu_control_1_control));
  EXMEM exmem_1 (
    .clk(counter_1_q[0]), .sumIn(somador_2_z), .zeroIn(alu_1_zero), .aluIn(alu_1_result),
    .read2In(idex_1_read2out), .wbAddIn(idex_1_wbaddout), .WBin(idex_1_wbout), .Min(idex_1_mout),
    .pcPl4In(idex_1_pcpl4out), .pcOut(exmem_1_pcout), .zeroOut(exmem_1_zeroout), .aluOut(exmem_1_aluout),
    .read2Out(exmem_1_read2out), .wbAddOut(exmem_1_wbaddout), .WBout(exmem_1_wbout),
    .Mout({or_1_out[1], exmem_1_mout}), .pcPl4Out(exmem_1_pcpl4out));
  or or_1 (or_1_out[0], exmem_1_mout[4], and_1_out);
  and and_1 (and_1_out, or_2_out, multiplexer_4_out);
  or or_2 (or_2_out, exmem_1_mout[2], exmem_1_mout[3]);
  Multiplexer multiplexer_4 (.in0(exmem_1_zeroout), .in1(not_1_out), .out(multiplexer_4_out), .sel(exmem_1_mout[3]));
  not not_1 (not_1_out, exmem_1_zeroout);
  RAM #(.addrWidth(24), .dataWidth(32)) ram_1 (
    .addr(exmem_1_aluout[23:0]), .we(exmem_1_mout[1]), .oe(exmem_1_mout[0]), .clk(clock_1_out),
    .din(exmem_1_read2out), .dout(ram_1_dout));
  MEMWB memwb_1 (
    .clk(counter_1_q[0]), .readIn(ram_1_dout), .aluIn(exmem_1_aluout), .wbAddIn(exmem_1_wbaddout),
    .WBin(exmem_1_wbout), .pcPl4In(exmem_1_pcpl4out), .pcPlIIn(exmem_1_pcout), .readOut(memwb_1_readout),
    .aluOut(memwb_1_aluout), .wbAddOut(memwb_1_wbaddout), .WBout(memwb_1_wbout), .pcPl4Out(memwb_1_pcpl4out),
    .pcPlIOut(memwb_1_pcpliout));
  Multiplexer #(.select(2), .width(32)) multiplexer_5 (
    .in0(memwb_1_aluout), .in1(memwb_1_readout), .in2(memwb_1_pcpl4out), .in3(memwb_1_pcpliout),
    .out(multiplexer_5_out), .sel(memwb_1_wbout[1:0]));

  // Notes on the sheet:
  //   contents of rom_1 (hex, n*v repeats v):
  //   9563
endmodule

// VHDL entity ALU, as the project stores it:
library IEEE;
use IEEE.STD_LOGIC_1164.ALL;
use ieee.numeric_std.ALL;
USE IEEE.std_logic_unsigned.ALL;

entity ALU is
    port(
    A, B       : in std_logic_vector(31 downto 0);
    control   : in std_logic_vector(3 downto 0);
    result    : out std_logic_vector(31 downto 0);
    zero      : out std_logic);
end ALU;

architecture TypeArchitecture of ALU is

signal zero_out   : std_logic_vector(32 downto 0);
signal result_out : std_logic_vector(31 downto 0);


begin
	
    result_out <= (A + B) when control = "0010" else
    			   (A - B) when control = "0110" else
    			   (A XOR B) when control = "0101" else
    			   (A OR B) when control = "0001" else
    			   (A AND B) when control = "0000" else
    			   (std_logic_vector(shift_left(unsigned(A), to_integer(unsigned(B))))) when control = "0011" else
    			   (std_logic_vector(shift_right(unsigned(A), to_integer(unsigned(B))))) when control = "0111";
        			
    result <= result_out;
    zero_out(0)<= '0';
    G2: for I in 1 to 32 generate
            zero_out(I) <= zero_out(I - 1) or result_out(I - 1);
    end generate;
    zero <= not zero_out(32);
end TypeArchitecture;

// VHDL entity ALU_Control, as the project stores it:
----------------------------------------------------------------------------------
library IEEE;
use IEEE.STD_LOGIC_1164.ALL;

entity ALU_Control is
    port(
        Functs    : IN std_logic_vector(3 downto 0);
        AluOp   : IN std_logic_vector(1 downto 0);
        Control : OUT std_logic_vector(3 downto 0)
        );
end ALU_Control;

architecture TypeArchitecture of ALU_Control is
begin

	control <= "0010" when AluOp = "00" else -- Etc
			 "0110" when AluOp = "01" else -- Branch
			 "0010" when Functs = "0000" else -- Add
			 "0110" when Functs = "1000" else -- Sub
			 "0011" when Functs = "0001" else -- Shift left
			 "0101" when Functs = "0100" else -- Xor
			 "0111" when Functs = "0101" else -- Shift Right
			 "0001" when Functs = "0110" else -- Or
			 "0000" when Functs = "0111"; -- And			 
	
end TypeArchitecture;

// VHDL entity Control_Unit, as the project stores it:
library IEEE;
use IEEE.STD_LOGIC_1164.ALL;


entity Control_Unit is
    port(
        opcode                     : IN  std_logic_vector(6 downto 0);
        AluSrc, blockA, RegWrite 	: OUT std_logic;
        MemRead, MemWrite, Branch  : OUT std_logic;
        BranchNotEq, BrIncond		: OUT std_logic;
        regToPC				: OUT std_logic;
        AluOp,regSrc			: OUT std_logic_vector(1 downto 0)
        );
end Control_Unit;

architecture TypeArchitecture of Control_Unit is

begin
	process(opcode)
	begin
	    	IF (opcode = "0110011") THEN -- R-Type sem imediato
            AluSrc      <= '0';
            blockA      <= '0';
            RegWrite    <= '1';
            MemRead     <= '0';
            MemWrite    <= '0';
            Branch      <= '0';
            AluOp       <= "10";
            regSrc      <= "00";
            BranchNotEq <= '0';
            BrIncond    <= '0';
            regToPC     <= '0';
        END IF;


        IF (opcode = "0010011") THEN -- R-Type com imediato
            AluSrc      <= '1';
            blockA      <= '0';
            RegWrite    <= '1';
            MemRead     <= '0';
            MemWrite    <= '0';
            Branch      <= '0';
            AluOp       <= "11";
            regSrc      <= "00";
            BranchNotEq <= '0';
            BrIncond    <= '0';
            regToPC     <= '0';
        END IF;


        IF (opcode = "0100011") THEN -- sw
            AluSrc      <= '1';
            blockA      <= '0';
            RegWrite    <= '0';
            MemRead     <= '0';
            MemWrite    <= '1';
            Branch      <= '0';
            AluOp       <= "00";
            regSrc      <= "00";
            BranchNotEq <= '0';
            BrIncond    <= '0';
            regToPC     <= '0';
        END IF;


        IF (opcode = "1100111") THEN -- beq
            AluSrc      <= '0';
            blockA      <= '0';
            RegWrite    <= '0';
            MemRead     <= '0';
            MemWrite    <= '0';
            Branch      <= '1';
            AluOp       <= "01";
            regSrc      <= "00";
            BranchNotEq <= '0';
            BrIncond    <= '0';
            regToPC     <= '0';
        END IF;


        IF (opcode = "1100011") THEN -- bnq
            AluSrc      <= '0';
            blockA      <= '0';
            RegWrite    <= '0';
            MemRead     <= '0';
            MemWrite    <= '0';
            Branch      <= '0';
            AluOp       <= "01";
            regSrc      <= "00";
            BranchNotEq <= '1';
            BrIncond    <= '0';
            regToPC     <= '0';
        END IF;


        IF (opcode = "1100110") THEN -- jalr
            AluSrc      <= '1';
            blockA      <= '0';
            RegWrite    <= '1';
            MemRead     <= '0';
            MemWrite    <= '0';
            Branch      <= '0';
            AluOp       <= "00";
            regSrc      <= "10";
            BranchNotEq <= '0';
            BrIncond    <= '1';
            regToPC     <= '1';
        END IF;


        IF (opcode = "1101111") THEN -- jal
            AluSrc      <= '1';
            blockA      <= '0';
            RegWrite    <= '1';
            MemRead     <= '0';
            MemWrite    <= '0';
            Branch      <= '0';
            AluOp       <= "00";
            regSrc      <= "10";
            BranchNotEq <= '0';
            BrIncond    <= '1';
            regToPC     <= '0';
        END IF;


        IF (opcode = "0000011") THEN -- lw
            AluSrc      <= '1';
            blockA      <= '0';
            RegWrite    <= '1';
            MemRead     <= '1';
            MemWrite    <= '0';
            Branch      <= '0';
            AluOp       <= "00";
            regSrc      <= "01";
            BranchNotEq <= '0';
            BrIncond    <= '0';
            regToPC     <= '0';
        END IF;


        IF (opcode = "0110111") THEN -- lui
            AluSrc      <= '1';
            blockA      <= '1';
            RegWrite    <= '1';
            MemRead     <= '0';
            MemWrite    <= '0';
            Branch      <= '0';
            AluOp       <= "00";
            regSrc      <= "00";
            BranchNotEq <= '0';
            BrIncond    <= '0';
            regToPC     <= '0';
        END IF;


        IF (opcode = "1110111") THEN -- auipc
            AluSrc      <= '1';
            blockA      <= '0';
            RegWrite    <= '1';
            MemRead     <= '0';
            MemWrite    <= '0';
            Branch      <= '0';
            AluOp       <= "00";
            regSrc      <= "11";
            BranchNotEq <= '0';
            BrIncond    <= '1';
            regToPC     <= '0';
        END IF;
	end process;
end TypeArchitecture;

// VHDL entity ImmGen, as the project stores it:
library IEEE;
use IEEE.STD_LOGIC_1164.ALL;
USE IEEE.NUMERIC_STD.ALL;

entity ImmGen is
    Port( 
        inst: in std_logic_vector(31 downto 0);
        imm: out std_logic_vector(31 downto 0));
end ImmGen;

architecture Behavioral of ImmGen is
signal opcode		: std_logic_vector(6 downto 0);
signal imm_interno 	: std_logic_vector(31 downto 0) := "00000000000000000000000000000000";

begin

opcode <= inst(6 downto 0);

process(opcode)
begin
	if (opcode = "0010011" or opcode = "1100110") then --I type
		imm_interno(11 downto 0)  <= inst(31 downto 20);
		imm_interno(31 downto 12) <= (others => inst(31));
	elsif (opcode = "1110111" or opcode = "0110111") then -- U type
		imm_interno(31 downto 12) <= inst(31 downto 12);
	elsif (opcode = "0100011") then -- S type
		imm_interno(11 downto 5) <= inst(31 downto 25);
		imm_interno(4 downto 0)  <= inst(11 downto 7);
		imm_interno(31 downto 12) <= (others => inst(31));
	elsif (opcode = "1100111" or opcode = "1100011") then -- SB type
		imm_interno(12) <= inst(31);
		imm_interno(11) <= inst(7);
		imm_interno(10 downto 5) <= inst(30 downto 25);
		imm_interno(4 downto 1) <= inst(11 downto 8);
		imm_interno(31 downto 13) <= (others => inst(31));
	elsif (opcode = "1101111") then -- UJ type
		imm_interno(20) <= inst(31);
		imm_interno(19 downto 12) <= inst(19 downto 12);
		imm_interno(11) <= inst(20);
		imm_interno(10 downto 1) <= inst(30 downto 21);
	end if;
end process;

imm <= imm_interno;

end Behavioral;

// VHDL entity PC2, as the project stores it:
LIBRARY ieee;
USE ieee.std_logic_1164.all;

ENTITY PC2 IS
  PORT (
  ------------------------------------------------------------------------------
  --Insert input ports below
    clk      : IN  std_logic;                    -- input bit example
    reset    : IN  std_logic;
    pc_in    : IN  std_logic_vector(31 DOWNTO 0); -- input vector example
  ------------------------------------------------------------------------------
  --Insert output ports below
    pc_out   : OUT std_logic_vector(31 DOWNTO 0)  -- output vector example
    );
END PC2;

--------------------------------------------------------------------------------
--Complete your VHDL description below
--------------------------------------------------------------------------------

ARCHITECTURE TypeArchitecture OF PC2 IS

BEGIN

	
	PROCESS (clk, reset)
	BEGIN
		IF (rising_edge(clk)) THEN
			if (pc_in = "UUUUUUUUUUUUUUUUUUUUUUUUUUUUUUUU") then
				pc_out <= (others => '0');
			else
				pc_out <= pc_in;
			end if;
		END IF;
		IF (reset = '1') THEN
			pc_out <= (others => '0');
		END IF;
	END PROCESS;

END TypeArchitecture;

// VHDL entity somador, as the project stores it:
LIBRARY ieee;
USE ieee.std_logic_1164.all;

USE IEEE.std_logic_unsigned.ALL;

ENTITY somador IS
  PORT (
  ------------------------------------------------------------------------------
    A, B        : IN  std_logic_vector(31 DOWNTO 0); -- input vector example
  ------------------------------------------------------------------------------
    Z           : OUT std_logic_vector(31 DOWNTO 0)  -- output vector example
    );
END somador;

ARCHITECTURE TypeArchitecture OF somador IS

BEGIN

Z <= A + B;

END TypeArchitecture;

// VHDL entity register_file, as the project stores it:
library ieee;
use ieee.std_logic_1164.all;
use ieee.numeric_std.all;

entity register_file is
  port(
    outA        : out std_logic_vector(31 downto 0);
    outB        : out std_logic_vector(31 downto 0);
    input       : in  std_logic_vector(31 downto 0);
    regSelManual: in  std_logic_vector(4 downto 0);
    outRegManual: out std_logic_vector(31 downto 0);
    writeEnable : in  std_logic;
    regASel     : in  std_logic_vector(4 downto 0);
    regBSel     : in  std_logic_vector(4 downto 0);
    writeRegSel : in  std_logic_vector(4 downto 0);
    clk         : in  std_logic
    );
end register_file;


architecture TypeArchitecture of register_file is
  type registerFile is array(0 to 31) of std_logic_vector(31 downto 0);
  signal registers : registerFile := 
   ("00000000000000000000000000010000","00000000000000000000000000000001","00000000000000000000000000000000","00000000000000000000000000000000",
    "00000000000000000000000000000000","00000000000000000000000000000000","00000000000000000000000000000000","00000000000000000000000000000000",
    "00000000000000000000000000000000","00000000000000000000000000000000","00000000000000000000000000000000","00000000000000000000000000000000",
    "00000000000000000000000000000000","00000000000000000000000000000000","00000000000000000000000000000000","00000000000000000000000000000000",
    "00000000000000000000000000000000","00000000000000000000000000000000","00000000000000000000000000000000","00000000000000000000000000000000",
    "00000000000000000000000000000000","00000000000000000000000000000000","00000000000000000000000000000000","00000000000000000000000000000000",
    "00000000000000000000000000000000","00000000000000000000000000000000","00000000000000000000000000000000","00000000000000000000000000000000",
    "00000000000000000000000000000000","00000000000000000000000000000000","00000000000000000000000000000000","00000000000000000000000000000000");
begin
regFile : process (clk) is
  begin
    if rising_edge(clk) then
      -- Read A and B before bypass
      if (registers(to_integer(unsigned(regASel))) = "UUUUUUUUUUUUUUUUUUUUUUUUUUUUUUUU") THEN
      	outA <= (others => '0');
      ELSE 
      	outA <= registers(to_integer(unsigned(regASel)));
      END IF;
      IF (registers(to_integer(unsigned(regBSel))) = "UUUUUUUUUUUUUUUUUUUUUUUUUUUUUUUU") THEN
      	outB <= (others => '0');
      ELSE
      	outB <= registers(to_integer(unsigned(regBSel)));
      END IF;
      -- Write and bypass
      if writeEnable = '1' then
        registers(to_integer(unsigned(writeRegSel))) <= input;  -- Write
        if regASel = writeRegSel then  -- Bypass for read A
          outA <= input;
        end if;
        if regBSel = writeRegSel then  -- Bypass for read B
          outB <= input;
        end if;
      end if;
    end if;
  end process;
  -- seleção manual
  outRegManual <= registers(to_integer(unsigned(regSelManual)));
  
end TypeArchitecture;

// VHDL entity IFID, as the project stores it:
LIBRARY ieee;
USE ieee.std_logic_1164.all;

ENTITY IFID IS
  PORT (
    clk         : IN  std_logic;                   
    pcIn        : IN  std_logic_vector(31 DOWNTO 0);
    pcPl4In	 : IN  std_logic_vector(31 downto 0);
    instIn      : IN  std_logic_vector(31 DOWNTO 0);
    pcOut       : OUT std_logic_vector(31 DOWNTO 0);   
    pcPl4Out	 : OUT std_logic_vector(31 downto 0);                 
    instOut     : OUT std_logic_vector(31 DOWNTO 0)
    );
END IFID;


ARCHITECTURE TypeArchitecture OF IFID IS

SIGNAL IDIF : std_logic_vector(95 DOWNTO 0);

BEGIN


	
	PROCESS (clk)
	BEGIN
		IF (rising_edge(clk)) THEN
			IDIF(31 DOWNTO 0) <= instIn;
			IDIF(63 DOWNTO 32) <= pcIn;
			IDIF(95 downto 64) <= pcPl4In;
		END IF;
		IF (falling_edge(clk)) THEN
			pcOut <= IDIF(63 DOWNTO 32);
			instOut <= IDIF(31 DOWNTO 0);
			pcPl4Out <= IDIF(95 downto 64);
		END IF;
	END PROCESS;

	
END TypeArchitecture;

// VHDL entity IDEX, as the project stores it:
LIBRARY ieee;
USE ieee.std_logic_1164.all;

ENTITY IDEX IS
  PORT (
    clk            : IN  std_logic;                   
    pcIn           : IN  std_logic_vector(31 DOWNTO 0);
    read1In        : IN  std_logic_vector(31 DOWNTO 0);
    read2In        : IN  std_logic_vector(31 DOWNTO 0);
    immGenIn       : in  std_logic_vector(31 DOWNTO 0);
    aluControlin   : IN  std_logic_vector(3 downto 0);
    wbAddIn        : IN  std_logic_vector(4 downto 0);
    WBin		    : IN  std_logic_vector(2 downto 0);
    Min 		    : IN  std_logic_vector(5 downto 0);
    EXin    	    : IN  std_logic_vector(3 downto 0);
    pcPl4In	    : IN  std_logic_vector(31 downto 0);
                        
    pcOut          : OUT std_logic_vector(31 DOWNTO 0);
    read1Out	    : OUT std_logic_vector(31 DOWNTO 0);
    read2Out       : OUT std_logic_vector(31 DOWNTO 0);
    immGenOut      : OUT std_logic_vector(31 DOWNTO 0);
    aluControlout  : OUT std_logic_vector(3 downto 0);
    wbAddOut       : OUT std_logic_vector(4 downto 0);
    WBout		    : OUT std_logic_vector(2 downto 0);
    Mout 		    : OUT std_logic_vector(5 downto 0);
    EXout    	    : OUT std_logic_vector(3 downto 0);
    pcPl4Out	    : OUT std_logic_vector(31 downto 0)
    );
END IDEX;


ARCHITECTURE TypeArchitecture OF IDEX IS

SIGNAL idex_s : std_logic_vector(181 DOWNTO 0);

BEGIN

	PROCESS (clk)
	BEGIN
		IF (rising_edge(clk)) THEN
			idex_s(31 DOWNTO 0)    <= pcIn;
			idex_s(63 DOWNTO 32)   <= read1In;
			idex_s(95 DOWNTO 64)   <= read2In;
			idex_s(127 DOWNTO 96)  <= immGenIn;
			idex_s(131 DOWNTO 128) <= aluControlin;
			idex_s(136 DOWNTO 132) <= wbAddIn;
			idex_s(139 downto 137) <= WBin;
			idex_s(145 downto 140) <= Min;
			idex_s(149 downto 146) <= EXin;
			idex_s(181 downto 150) <= pcPl4In;
		END IF;
		IF (falling_edge(clk)) THEN
			pcOut    <= idex_s(31 DOWNTO 0);
			read1Out  <= idex_s(63 DOWNTO 32);
			read2Out  <= idex_s(95 DOWNTO 64);
			immGenOut <= idex_s(127 DOWNTO 96);
			aluControlout <= idex_s(131 DOWNTO 128);
			wbAddOut <= idex_s(136 DOWNTO 132);
			WBout <= idex_s(139 downto 137);
			Mout <= idex_s(145 downto 140);
			EXout <= idex_s(149 downto 146);
			pcPl4Out <= idex_s(181 downto 150);
		END IF;
	END PROCESS;

	
END TypeArchitecture;

// VHDL entity EXMEM, as the project stores it:
LIBRARY ieee;
USE ieee.std_logic_1164.all;

ENTITY EXMEM IS
  PORT (
    clk            : IN  std_logic;                   
    sumIn           : IN  std_logic_vector(31 DOWNTO 0);
    zeroIn        : IN  std_logic;
    aluIn        : IN  std_logic_vector(31 DOWNTO 0);
    read2In       : in  std_logic_vector(31 DOWNTO 0);
    wbAddIn        : IN  std_logic_vector(4 downto 0);
    WBin		    : IN  std_logic_vector(2 downto 0);
    Min 		    : IN  std_logic_vector(5 downto 0);
    pcPl4In	    : IN std_logic_vector(31 downto 0);
    
                        
    pcOut         : OUT std_logic_vector(31 DOWNTO 0);
    zeroOut	    : OUT std_logic;
    aluOut       : OUT std_logic_vector(31 DOWNTO 0);
    read2Out      : OUT std_logic_vector(31 DOWNTO 0);
    wbAddOut       : OUT std_logic_vector(4 downto 0);
    WBout		    : OUT std_logic_vector(2 downto 0);
    Mout 		    : OUT std_logic_vector(5 downto 0);
    pcPl4Out	    : OUT std_logic_vector(31 downto 0)
    );
END EXMEM;


ARCHITECTURE TypeArchitecture OF EXMEM IS

SIGNAL exmem_s : std_logic_vector(142 DOWNTO 0);

BEGIN

	PROCESS (clk)
	BEGIN
		IF (rising_edge(clk)) THEN
			exmem_s(31 DOWNTO 0)   <= sumIn;
			exmem_s(32)  <= zeroIn;
			exmem_s(64 DOWNTO 33)  <= aluIn;
			exmem_s(96 DOWNTO 65) <= read2In;
			exmem_s(101 DOWNTO 97) <= wbAddIn;
			exmem_s(104 DOWNTO 102) <= WBin;
			exmem_s(110 DOWNTO 105) <= Min;
			exmem_s(142 downto 111) <= pcPl4In;
		END IF;
		IF (falling_edge(clk)) THEN
			pcOut    <=  exmem_s(31 DOWNTO 0);
			
			if (exmem_s(32) = 'U') then
				zeroOut <= '0';
			else
				zeroOut <= exmem_s(32);
			end if; 

			if (exmem_s(64 DOWNTO 33) = "UUUUUUUUUUUUUUUUUUUUUUUUUUUUUUUU") then
				aluOut <= "00000000000000000000000000000000";
			else
				aluOut <= exmem_s(64 DOWNTO 33);
			end if;
			
			read2Out <= exmem_s(96 DOWNTO 65);
			wbAddOut <= exmem_s(101 DOWNTO 97);
			
			if (exmem_s(109 DOWNTO 105) = "UUUUUU") then
				Mout <= "000000";
			else
				Mout <= exmem_s(110 DOWNTO 105);
			end if;
			
			WBout <= exmem_s(104 DOWNTO 102);

			pcPl4Out <= exmem_s(142 downto 111);
			
			
		END IF;
	END PROCESS;

	
END TypeArchitecture;

// VHDL entity MEMWB, as the project stores it:
LIBRARY ieee;
USE ieee.std_logic_1164.all;

ENTITY MEMWB IS
  PORT (
    clk            : IN  std_logic;                   
    readIn           : IN  std_logic_vector(31 DOWNTO 0);
    aluIn        : IN  std_logic_vector(31 DOWNTO 0);
    wbAddIn        : IN  std_logic_vector(4 downto 0);
    WBin		    : IN  std_logic_vector(2 downto 0);
    pcPl4In	    : IN std_logic_vector(31 downto 0);
    pcPlIIn	    : IN std_logic_vector(31 downto 0);
                        
    readOut         : OUT std_logic_vector(31 DOWNTO 0);
    aluOut	    : OUT std_logic_vector(31 DOWNTO 0);
    wbAddOut       : OUT std_logic_vector(4 downto 0);
    WBout		    : OUT std_logic_vector(2 downto 0);
    pcPl4Out       : OUT std_logic_vector(31 downto 0);
    pcPlIOut	    : Out std_logic_vector(31 downto 0)
    );
END MEMWB;


ARCHITECTURE TypeArchitecture OF MEMWB IS

SIGNAL memwb_s : std_logic_vector(135 DOWNTO 0);

BEGIN

	PROCESS (clk)
	BEGIN
		IF (rising_edge(clk)) THEN
			memwb_s(31 DOWNTO 0)   <= readIn;
			memwb_s(63 DOWNTO 32)  <= aluIn;
			memwb_s(68 DOWNTO 64)  <= wbAddIn;
			memwb_s(71 DOWNTO 69)  <= WBin;
			memwb_s(103 downto 72) <= pcPl4In;
			memwb_s(135 downto 104) <= pcPlIIn;
			
		END IF;
		IF (falling_edge(clk)) THEN
			readOut    <=  memwb_s(31 DOWNTO 0);
			aluOut  <=  memwb_s(63 DOWNTO 32);
			wbAddOut <= memwb_s(68 DOWNTO 64);
			WBout <= memwb_s(71 DOWNTO 69);
			pcPl4Out <= memwb_s(103 downto 72);
			pcPlIOut <= memwb_s(135 downto 104);
		END IF;
	END PROCESS;

	
END TypeArchitecture;
