// Logisim project SomadorComVHDL.circ as structural Verilog
module main (
  input  [31:0] B_i,
  input  [31:0] A_i,
  input  mode_i,
  input  [1:0] vecSize_i,
  output [31:0] out_5,
  output [31:0] S_i
);

  wire and_1_out, and_2_out, and_3_out, and_4_out, and_5_out, and_6_out, and_7_out, and_8_out, and_10_out,
       and_11_out, and_12_out, and_13_out, and_14_out, and_15_out, carry01, carry34, fa_1_c_out, fa_2_c_out,
       fa_3_c_out, fa_4_c_out, fa_5_c_out, fa_6_c_out, fa_7_c_out, fa_8_c_out, fa_9_c_out, fa_10_c_out,
       fa_11_c_out, fa_12_c_out, fa_13_c_out, fa_14_c_out, fa_15_c_out, fa_16_c_out, fa_17_c_out,
       fa_18_c_out, fa_19_c_out, fa_20_c_out, fa_21_c_out, fa_22_c_out, fa_23_c_out, fa_24_c_out,
       fa_25_c_out, fa_26_c_out, fa_27_c_out, fa_28_c_out, fa_29_c_out, fa_30_c_out, fa_31_c_out, not_2_out,
       not_3_out, not_4_out, not_5_out, not_6_out, not_7_out, not_8_out, or_1_out, or_2_out, or_4_out,
       or_5_out, or_6_out, or_7_out, or_8_out;
  wire [3:0] multiplexer_1_out_2, multiplexer_1_out_3, multiplexer_1_out_4, multiplexer_1_out_5,
       multiplexer_1_out_6;
  wire [23:0] multiplexer_1_out;
  wire [31:0] not_1_out;

  SomadorVetorial somadorvetorial_1 (.A_i(A_i), .B_i(B_i), .vecSize_i(vecSize_i), .mode_i(mode_i), .S_i(S_i));
  Multiplexer #(.width(32)) multiplexer_1 (
    .in0(B_i), .in1(not_1_out),
    .out({multiplexer_1_out_6, multiplexer_1_out_5, multiplexer_1_out[23:16], multiplexer_1_out_4, multiplexer_1_out_3, multiplexer_1_out_2, multiplexer_1_out[3:0]}),
    .sel(mode_i));
  assign not_1_out = ~B_i;  // NOT_Gate not_1, 32 bits wide
  FA fa_1 (.A(A_i[0]), .B(multiplexer_1_out[0]), .C_in(mode_i), .SUM(out_5[0]), .C_out(fa_1_c_out));
  FA fa_2 (.A(A_i[1]), .B(multiplexer_1_out[1]), .C_in(fa_1_c_out), .SUM(out_5[1]), .C_out(fa_2_c_out));
  FA fa_3 (.A(A_i[2]), .B(multiplexer_1_out[2]), .C_in(fa_2_c_out), .SUM(out_5[2]), .C_out(fa_3_c_out));
  FA fa_4 (.A(A_i[3]), .B(multiplexer_1_out[3]), .C_in(fa_3_c_out), .SUM(out_5[3]), .C_out(fa_4_c_out));
  and and_1 (and_1_out, fa_4_c_out, carry01);
  not not_2 (not_2_out, carry01);
  and and_2 (and_2_out, not_2_out, mode_i);
  FA fa_5 (.A(A_i[16]), .B(multiplexer_1_out[16]), .C_in(or_7_out), .SUM(out_5[16]), .C_out(fa_5_c_out));
  FA fa_6 (.A(A_i[17]), .B(multiplexer_1_out[17]), .C_in(fa_5_c_out), .SUM(out_5[17]), .C_out(fa_6_c_out));
  FA fa_7 (.A(A_i[18]), .B(multiplexer_1_out[18]), .C_in(fa_6_c_out), .SUM(out_5[18]), .C_out(fa_7_c_out));
  FA fa_8 (.A(A_i[19]), .B(multiplexer_1_out[19]), .C_in(fa_7_c_out), .SUM(out_5[19]), .C_out(fa_8_c_out));
  not not_3 (not_3_out, carry01);
  or or_1 (or_1_out, and_1_out, and_2_out);
  or or_2 (or_2_out, and_3_out, and_4_out);
  and and_3 (and_3_out, fa_8_c_out, carry01);
  and and_4 (and_4_out, not_3_out, mode_i);
  FA fa_9 (.A(A_i[4]), .B(multiplexer_1_out_2[0]), .C_in(or_1_out), .SUM(out_5[4]), .C_out(fa_9_c_out));
  FA fa_10 (.A(A_i[5]), .B(multiplexer_1_out_2[1]), .C_in(fa_9_c_out), .SUM(out_5[5]), .C_out(fa_10_c_out));
  FA fa_11 (.A(A_i[6]), .B(multiplexer_1_out_2[2]), .C_in(fa_10_c_out), .SUM(out_5[6]), .C_out(fa_11_c_out));
  FA fa_12 (.A(A_i[7]), .B(multiplexer_1_out_2[3]), .C_in(fa_11_c_out), .SUM(out_5[7]), .C_out(fa_12_c_out));
  not not_4 (not_4_out, vecSize_i[1]);
  FA fa_13 (.A(A_i[20]), .B(multiplexer_1_out[20]), .C_in(or_2_out), .SUM(out_5[20]), .C_out(fa_13_c_out));
  FA fa_14 (.A(A_i[21]), .B(multiplexer_1_out[21]), .C_in(fa_13_c_out), .SUM(out_5[21]), .C_out(fa_14_c_out));
  FA fa_15 (.A(A_i[22]), .B(multiplexer_1_out[22]), .C_in(fa_14_c_out), .SUM(out_5[22]), .C_out(fa_15_c_out));
  FA fa_16 (.A(A_i[23]), .B(multiplexer_1_out[23]), .C_in(fa_15_c_out), .SUM(out_5[23]), .C_out(fa_16_c_out));
  not not_5 (not_5_out, vecSize_i[1]);
  and and_5 (and_5_out, fa_12_c_out, vecSize_i[1]);
  and and_6 (and_6_out, not_4_out, mode_i);
  and and_7 (and_7_out, fa_16_c_out, vecSize_i[1]);
  and and_8 (and_8_out, not_5_out, mode_i);
  or or_3 (carry01, vecSize_i[0], vecSize_i[1]);
  and and_9 (carry34, vecSize_i[0], vecSize_i[1]);
  or or_4 (or_4_out, and_5_out, and_6_out);
  or or_5 (or_5_out, and_7_out, and_8_out);
  FA fa_17 (.A(A_i[8]), .B(multiplexer_1_out_3[0]), .C_in(or_4_out), .SUM(out_5[8]), .C_out(fa_17_c_out));
  FA fa_18 (.A(A_i[9]), .B(multiplexer_1_out_3[1]), .C_in(fa_17_c_out), .SUM(out_5[9]), .C_out(fa_18_c_out));
  FA fa_19 (.A(A_i[10]), .B(multiplexer_1_out_3[2]), .C_in(fa_18_c_out), .SUM(out_5[10]), .C_out(fa_19_c_out));
  FA fa_20 (.A(A_i[11]), .B(multiplexer_1_out_3[3]), .C_in(fa_19_c_out), .SUM(out_5[11]), .C_out(fa_20_c_out));
  FA fa_21 (.A(A_i[24]), .B(multiplexer_1_out_5[0]), .C_in(or_5_out), .SUM(out_5[24]), .C_out(fa_21_c_out));
  FA fa_22 (.A(A_i[25]), .B(multiplexer_1_out_5[1]), .C_in(fa_21_c_out), .SUM(out_5[25]), .C_out(fa_22_c_out));
  FA fa_23 (.A(A_i[26]), .B(multiplexer_1_out_5[2]), .C_in(fa_22_c_out), .SUM(out_5[26]), .C_out(fa_23_c_out));
  FA fa_24 (.A(A_i[27]), .B(multiplexer_1_out_5[3]), .C_in(fa_23_c_out), .SUM(out_5[27]), .C_out(fa_24_c_out));
  and and_10 (and_10_out, fa_20_c_out, carry01);
  not not_6 (not_6_out, carry01);
  and and_11 (and_11_out, not_6_out, mode_i);
  and and_12 (and_12_out, fa_24_c_out, carry01);
  not not_7 (not_7_out, carry01);
  and and_13 (and_13_out, not_7_out, mode_i);
  or or_6 (or_6_out, and_10_out, and_11_out);
  or or_7 (or_7_out, and_14_out, and_15_out);
  or or_8 (or_8_out, and_12_out, and_13_out);
  and and_14 (and_14_out, mode_i, not_8_out);
  not not_8 (not_8_out, carry34);
  FA fa_25 (.A(A_i[12]), .B(multiplexer_1_out_4[0]), .C_in(or_6_out), .SUM(out_5[12]), .C_out(fa_25_c_out));
  FA fa_26 (.A(A_i[13]), .B(multiplexer_1_out_4[1]), .C_in(fa_25_c_out), .SUM(out_5[13]), .C_out(fa_26_c_out));
  FA fa_27 (.A(A_i[14]), .B(multiplexer_1_out_4[2]), .C_in(fa_26_c_out), .SUM(out_5[14]), .C_out(fa_27_c_out));
  FA fa_28 (.A(A_i[15]), .B(multiplexer_1_out_4[3]), .C_in(fa_27_c_out), .SUM(out_5[15]), .C_out(fa_28_c_out));
  FA fa_29 (.A(A_i[28]), .B(multiplexer_1_out_6[0]), .C_in(or_8_out), .SUM(out_5[28]), .C_out(fa_29_c_out));
  FA fa_30 (.A(A_i[29]), .B(multiplexer_1_out_6[1]), .C_in(fa_29_c_out), .SUM(out_5[29]), .C_out(fa_30_c_out));
  FA fa_31 (.A(A_i[30]), .B(multiplexer_1_out_6[2]), .C_in(fa_30_c_out), .SUM(out_5[30]), .C_out(fa_31_c_out));
  FA fa_32 (.A(A_i[31]), .B(multiplexer_1_out_6[3]), .C_in(fa_31_c_out), .SUM(out_5[31]));  // open: C_out
  and and_15 (and_15_out, fa_28_c_out, carry34);

  // Other names for the same wires on the sheet: negation = mode_i; carry12 = vecSize_i[1]
endmodule

module FA (
  input  A,
  input  B,
  input  C_in,
  output SUM,
  output C_out
);

  wire and_1_out, and_2_out, and_3_out, xor_1_out;

  and and_1 (and_1_out, A, B);
  and and_2 (and_2_out, A, C_in);
  and and_3 (and_3_out, B, C_in);
  xor xor_1 (xor_1_out, A, B);
  or or_1 (C_out, and_1_out, and_2_out, and_3_out);
  xor xor_2 (SUM, xor_1_out, C_in);
endmodule

module somVetorial (
  input  [31:0] in_1,
  input  [31:0] in_2,
  input  [1:0] in_3,
  input  _0___soma,
  output [31:0] out_5
);

  SomadorVetorial somadorvetorial_1 (.A_i(in_1), .B_i(in_2), .vecSize_i(in_3), .mode_i(_0___soma), .S_i(out_5));

  // Notes on the sheet:
  //   11 - bit a bit
  //   10 - 16 bits
  //   01 - 8 bits
  //   00 - 4 bits
  //   1 - subtracao
endmodule

// VHDL entity SomadorVetorial, as the project stores it:
LIBRARY ieee;
USE ieee.std_logic_1164.all;

ENTITY SomadorVetorial IS
  PORT (
  ------------------------------------------------------------------------------  
    A_i, B_i   : IN  std_logic_vector (31 DOWNTO 0);                    
    vecSize_i  : In  std_logic_vector (1 DOWNTO 0);
    mode_i     : IN  std_logic; 
  ------------------------------------------------------------------------------
    S_i        : OUT std_logic_vector (31 downto 0)
    );
END SomadorVetorial;

--------------------------------------------------------------------------------
--Complete your VHDL description below
--------------------------------------------------------------------------------

ARCHITECTURE TypeArchitecture OF SomadorVetorial IS
-- Sinal para representar um módulo Carry-Lookahead
SIGNAL C_cla : std_logic_vector (31 DOWNTO 0);
-- Sinal para representar as permissões de propagação de carry
SIGNAL perm  : std_logic_vector (2 DOWNTO 0);
-- Sinal para armazenar o valor que iremos utilizar para B na operação
SIGNAL B_u   : std_logic_vector (31 DOWNTO 0);
BEGIN

-- Definindo B_u (B_utilizável)
B_u(0) <= (B_i(0) and (not mode_i)) or ((not B_i(0)) and mode_i);
B_u(1) <= (B_i(1) and (not mode_i)) or ((not B_i(1)) and mode_i);
B_u(2) <= (B_i(2) and (not mode_i)) or ((not B_i(2)) and mode_i);
B_u(3) <= (B_i(3) and (not mode_i)) or ((not B_i(3)) and mode_i);
B_u(4) <= (B_i(4) and (not mode_i)) or ((not B_i(4)) and mode_i);
B_u(5) <= (B_i(5) and (not mode_i)) or ((not B_i(5)) and mode_i);
B_u(6) <= (B_i(6) and (not mode_i)) or ((not B_i(6)) and mode_i);
B_u(7) <= (B_i(7) and (not mode_i)) or ((not B_i(7)) and mode_i);
B_u(8) <= (B_i(8) and (not mode_i)) or ((not B_i(8)) and mode_i);
B_u(9) <= (B_i(9) and (not mode_i)) or ((not B_i(9)) and mode_i);
B_u(10) <= (B_i(10) and (not mode_i)) or ((not B_i(10)) and mode_i);
B_u(11) <= (B_i(11) and (not mode_i)) or ((not B_i(11)) and mode_i);
B_u(12) <= (B_i(12) and (not mode_i)) or ((not B_i(12)) and mode_i);
B_u(13) <= (B_i(13) and (not mode_i)) or ((not B_i(13)) and mode_i);
B_u(14) <= (B_i(14) and (not mode_i)) or ((not B_i(14)) and mode_i);
B_u(15) <= (B_i(15) and (not mode_i)) or ((not B_i(15)) and mode_i);
B_u(16) <= (B_i(16) and (not mode_i)) or ((not B_i(16)) and mode_i);
B_u(17) <= (B_i(17) and (not mode_i)) or ((not B_i(17)) and mode_i);
B_u(18) <= (B_i(18) and (not mode_i)) or ((not B_i(18)) and mode_i);
B_u(19) <= (B_i(19) and (not mode_i)) or ((not B_i(19)) and mode_i);
B_u(20) <= (B_i(20) and (not mode_i)) or ((not B_i(20)) and mode_i);
B_u(21) <= (B_i(21) and (not mode_i)) or ((not B_i(21)) and mode_i);
B_u(22) <= (B_i(22) and (not mode_i)) or ((not B_i(22)) and mode_i);
B_u(23) <= (B_i(23) and (not mode_i)) or ((not B_i(23)) and mode_i);
B_u(24) <= (B_i(24) and (not mode_i)) or ((not B_i(24)) and mode_i);
B_u(25) <= (B_i(25) and (not mode_i)) or ((not B_i(25)) and mode_i);
B_u(26) <= (B_i(26) and (not mode_i)) or ((not B_i(26)) and mode_i);
B_u(27) <= (B_i(27) and (not mode_i)) or ((not B_i(27)) and mode_i);
B_u(28) <= (B_i(28) and (not mode_i)) or ((not B_i(28)) and mode_i);
B_u(29) <= (B_i(29) and (not mode_i)) or ((not B_i(29)) and mode_i);
B_u(30) <= (B_i(30) and (not mode_i)) or ((not B_i(30)) and mode_i);
B_u(31) <= (B_i(31) and (not mode_i)) or ((not B_i(31)) and mode_i);

-- Definindo perm
perm(0) <= vecSize_i(0) or vecSize_i(1);
perm(1) <= vecSize_i(1);
perm(2) <= vecSize_i(0) and vecSize_i(1);

C_cla(0) <= mode_i;
C_cla(1) <= (A_i(0) and B_u(0)) or ((A_i(0) or B_u(0)) and (mode_i));
C_cla(2) <= (A_i(1) and B_u(1)) or ((A_i(1) or B_u(1)) and ((A_i(0) and B_u(0)) or ((A_i(0) or B_u(0)) and (mode_i))));
C_cla(3) <= (A_i(2) and B_u(2)) or ((A_i(2) or B_u(2)) and ((A_i(1) and B_u(1)) or ((A_i(1) or B_u(1)) and ((A_i(0) and B_u(0)) or ((A_i(0) or B_u(0)) and (mode_i))))));
-- Subcampo 1 de 4 bits
C_cla(4) <= (((A_i(3) and B_u(3)) or ((A_i(3) or B_u(3)) and ((A_i(2) and B_u(2)) or ((A_i(2) or B_u(2)) and ((A_i(1) and B_u(1)) or ((A_i(1) or B_u(1)) and ((A_i(0) and B_u(0)) or ((A_i(0) or B_u(0)) and (mode_i))))))))) and perm(0)) or (mode_i and (not perm(0)));
C_cla(5) <= (A_i(4) and B_u(4)) or ((A_i(4) or B_u(4)) and ((((A_i(3) and B_u(3)) or ((A_i(3) or B_u(3)) and ((A_i(2) and B_u(2)) or ((A_i(2) or B_u(2)) and ((A_i(1) and B_u(1)) or ((A_i(1) or B_u(1)) and ((A_i(0) and B_u(0)) or ((A_i(0) or B_u(0)) and (mode_i))))))))) and perm(0)) or (mode_i and (not perm(0)))));
C_cla(6) <= (A_i(5) and B_u(5)) or ((A_i(5) or B_u(5)) and ((A_i(4) and B_u(4)) or ((A_i(4) or B_u(4)) and ((((A_i(3) and B_u(3)) or ((A_i(3) or B_u(3)) and ((A_i(2) and B_u(2)) or ((A_i(2) or B_u(2)) and ((A_i(1) and B_u(1)) or ((A_i(1) or B_u(1)) and ((A_i(0) and B_u(0)) or ((A_i(0) or B_u(0)) and (mode_i))))))))) and perm(0)) or (mode_i and (not perm(0)))))));
C_cla(7) <= (A_i(6) and B_u(6)) or ((A_i(6) or B_u(6)) and ((A_i(5) and B_u(5)) or ((A_i(5) or B_u(5)) and ((A_i(4) and B_u(4)) or ((A_i(4) or B_u(4)) and ((((A_i(3) and B_u(3)) or ((A_i(3) or B_u(3)) and ((A_i(2) and B_u(2)) or ((A_i(2) or B_u(2)) and ((A_i(1) and B_u(1)) or ((A_i(1) or B_u(1)) and ((A_i(0) and B_u(0)) or ((A_i(0) or B_u(0)) and (mode_i))))))))) and perm(0)) or (mode_i and (not perm(0)))))))));
-- Subcampo 2 de 4 bits
C_cla(8) <= (((A_i(7) and B_u(7)) or ((A_i(7) or B_u(7)) and ((A_i(6) and B_u(6)) or ((A_i(6) or B_u(6)) and ((A_i(5) and B_u(5)) or ((A_i(5) or B_u(5)) and ((A_i(4) and B_u(4)) or ((A_i(4) or B_u(4)) and ((((A_i(3) and B_u(3)) or ((A_i(3) or B_u(3)) and ((A_i(2) and B_u(2)) or ((A_i(2) or B_u(2)) and ((A_i(1) and B_u(1)) or ((A_i(1) or B_u(1)) and ((A_i(0) and B_u(0)) or ((A_i(0) or B_u(0)) and (mode_i))))))))) and perm(0)) or (mode_i and (not perm(0)))))))))))) and perm(1)) or (mode_i and (not perm(1)));
C_cla(9) <= (A_i(8) and B_u(8)) or ((A_i(8) or B_u(8)) and ((((A_i(7) and B_u(7)) or ((A_i(7) or B_u(7)) and ((A_i(6) and B_u(6)) or ((A_i(6) or B_u(6)) and ((A_i(5) and B_u(5)) or ((A_i(5) or B_u(5)) and ((A_i(4) and B_u(4)) or ((A_i(4) or B_u(4)) and ((((A_i(3) and B_u(3)) or ((A_i(3) or B_u(3)) and ((A_i(2) and B_u(2)) or ((A_i(2) or B_u(2)) and ((A_i(1) and B_u(1)) or ((A_i(1) or B_u(1)) and ((A_i(0) and B_u(0)) or ((A_i(0) or B_u(0)) and (mode_i))))))))) and perm(0)) or (mode_i and (not perm(0)))))))))))) and perm(1)) or (mode_i and (not perm(1)))));
C_cla(10) <= (A_i(9) and B_u(9)) or ((A_i(9) or B_u(9)) and ((A_i(8) and B_u(8)) or ((A_i(8) or B_u(8)) and ((((A_i(7) and B_u(7)) or ((A_i(7) or B_u(7)) and ((A_i(6) and B_u(6)) or ((A_i(6) or B_u(6)) and ((A_i(5) and B_u(5)) or ((A_i(5) or B_u(5)) and ((A_i(4) and B_u(4)) or ((A_i(4) or B_u(4)) and ((((A_i(3) and B_u(3)) or ((A_i(3) or B_u(3)) and ((A_i(2) and B_u(2)) or ((A_i(2) or B_u(2)) and ((A_i(1) and B_u(1)) or ((A_i(1) or B_u(1)) and ((A_i(0) and B_u(0)) or ((A_i(0) or B_u(0)) and (mode_i))))))))) and perm(0)) or (mode_i and (not perm(0)))))))))))) and perm(1)) or (mode_i and (not perm(1)))))));
C_cla(11) <= (A_i(10) and B_u(10)) or ((A_i(10) or B_u(10)) and ((A_i(9) and B_u(9)) or ((A_i(9) or B_u(9)) and ((A_i(8) and B_u(8)) or ((A_i(8) or B_u(8)) and ((((A_i(7) and B_u(7)) or ((A_i(7) or B_u(7)) and ((A_i(6) and B_u(6)) or ((A_i(6) or B_u(6)) and ((A_i(5) and B_u(5)) or ((A_i(5) or B_u(5)) and ((A_i(4) and B_u(4)) or ((A_i(4) or B_u(4)) and ((((A_i(3) and B_u(3)) or ((A_i(3) or B_u(3)) and ((A_i(2) and B_u(2)) or ((A_i(2) or B_u(2)) and ((A_i(1) and B_u(1)) or ((A_i(1) or B_u(1)) and ((A_i(0) and B_u(0)) or ((A_i(0) or B_u(0)) and (mode_i))))))))) and perm(0)) or (mode_i and (not perm(0)))))))))))) and perm(1)) or (mode_i and (not perm(1)))))))));
-- Subcampo 3 de 4 bits
C_cla(12) <= (((A_i(11) and B_u(11)) or ((A_i(11) or B_u(11)) and ((A_i(10) and B_u(10)) or ((A_i(10) or B_u(10)) and ((A_i(9) and B_u(9)) or ((A_i(9) or B_u(9)) and ((A_i(8) and B_u(8)) or ((A_i(8) or B_u(8)) and ((((A_i(7) and B_u(7)) or ((A_i(7) or B_u(7)) and ((A_i(6) and B_u(6)) or ((A_i(6) or B_u(6)) and ((A_i(5) and B_u(5)) or ((A_i(5) or B_u(5)) and ((A_i(4) and B_u(4)) or ((A_i(4) or B_u(4)) and ((((A_i(3) and B_u(3)) or ((A_i(3) or B_u(3)) and ((A_i(2) and B_u(2)) or ((A_i(2) or B_u(2)) and ((A_i(1) and B_u(1)) or ((A_i(1) or B_u(1)) and ((A_i(0) and B_u(0)) or ((A_i(0) or B_u(0)) and (mode_i))))))))) and perm(0)) or (mode_i and (not perm(0)))))))))))) and perm(1)) or (mode_i and (not perm(1)))))))))))) and perm(0)) or (mode_i and (not perm(0)));
C_cla(13) <= (A_i(12) and B_u(12)) or ((A_i(12) or B_u(12)) and ((((A_i(11) and B_u(11)) or ((A_i(11) or B_u(11)) and ((A_i(10) and B_u(10)) or ((A_i(10) or B_u(10)) and ((A_i(9) and B_u(9)) or ((A_i(9) or B_u(9)) and ((A_i(8) and B_u(8)) or ((A_i(8) or B_u(8)) and ((((A_i(7) and B_u(7)) or ((A_i(7) or B_u(7)) and ((A_i(6) and B_u(6)) or ((A_i(6) or B_u(6)) and ((A_i(5) and B_u(5)) or ((A_i(5) or B_u(5)) and ((A_i(4) and B_u(4)) or ((A_i(4) or B_u(4)) and ((((A_i(3) and B_u(3)) or ((A_i(3) or B_u(3)) and ((A_i(2) and B_u(2)) or ((A_i(2) or B_u(2)) and ((A_i(1) and B_u(1)) or ((A_i(1) or B_u(1)) and ((A_i(0) and B_u(0)) or ((A_i(0) or B_u(0)) and (mode_i))))))))) and perm(0)) or (mode_i and (not perm(0)))))))))))) and perm(1)) or (mode_i and (not perm(1)))))))))))) and perm(0)) or (mode_i and (not perm(0)))));
C_cla(14) <= (A_i(13) and B_u(13)) or ((A_i(13) or B_u(13)) and ((A_i(12) and B_u(12)) or ((A_i(12) or B_u(12)) and ((((A_i(11) and B_u(11)) or ((A_i(11) or B_u(11)) and ((A_i(10) and B_u(10)) or ((A_i(10) or B_u(10)) and ((A_i(9) and B_u(9)) or ((A_i(9) or B_u(9)) and ((A_i(8) and B_u(8)) or ((A_i(8) or B_u(8)) and ((((A_i(7) and B_u(7)) or ((A_i(7) or B_u(7)) and ((A_i(6) and B_u(6)) or ((A_i(6) or B_u(6)) and ((A_i(5) and B_u(5)) or ((A_i(5) or B_u(5)) and ((A_i(4) and B_u(4)) or ((A_i(4) or B_u(4)) and ((((A_i(3) and B_u(3)) or ((A_i(3) or B_u(3)) and ((A_i(2) and B_u(2)) or ((A_i(2) or B_u(2)) and ((A_i(1) and B_u(1)) or ((A_i(1) or B_u(1)) and ((A_i(0) and B_u(0)) or ((A_i(0) or B_u(0)) and (mode_i))))))))) and perm(0)) or (mode_i and (not perm(0)))))))))))) and perm(1)) or (mode_i and (not perm(1)))))))))))) and perm(0)) or (mode_i and (not perm(0)))))));
C_cla(15) <= (A_i(14) and B_u(14)) or ((A_i(14) or B_u(14)) and ((A_i(13) and B_u(13)) or ((A_i(13) or B_u(13)) and ((A_i(12) and B_u(12)) or ((A_i(12) or B_u(12)) and ((((A_i(11) and B_u(11)) or ((A_i(11) or B_u(11)) and ((A_i(10) and B_u(10)) or ((A_i(10) or B_u(10)) and ((A_i(9) and B_u(9)) or ((A_i(9) or B_u(9)) and ((A_i(8) and B_u(8)) or ((A_i(8) or B_u(8)) and ((((A_i(7) and B_u(7)) or ((A_i(7) or B_u(7)) and ((A_i(6) and B_u(6)) or ((A_i(6) or B_u(6)) and ((A_i(5) and B_u(5)) or ((A_i(5) or B_u(5)) and ((A_i(4) and B_u(4)) or ((A_i(4) or B_u(4)) and ((((A_i(3) and B_u(3)) or ((A_i(3) or B_u(3)) and ((A_i(2) and B_u(2)) or ((A_i(2) or B_u(2)) and ((A_i(1) and B_u(1)) or ((A_i(1) or B_u(1)) and ((A_i(0) and B_u(0)) or ((A_i(0) or B_u(0)) and (mode_i))))))))) and perm(0)) or (mode_i and (not perm(0)))))))))))) and perm(1)) or (mode_i and (not perm(1)))))))))))) and perm(0)) or (mode_i and (not perm(0)))))))));
-- Subcampo 4 de 4 bits
C_cla(16) <= (((A_i(15) and B_u(15)) or ((A_i(15) or B_u(15)) and ((A_i(14) and B_u(14)) or ((A_i(14) or B_u(14)) and ((A_i(13) and B_u(13)) or ((A_i(13) or B_u(13)) and ((A_i(12) and B_u(12)) or ((A_i(12) or B_u(12)) and ((((A_i(11) and B_u(11)) or ((A_i(11) or B_u(11)) and ((A_i(10) and B_u(10)) or ((A_i(10) or B_u(10)) and ((A_i(9) and B_u(9)) or ((A_i(9) or B_u(9)) and ((A_i(8) and B_u(8)) or ((A_i(8) or B_u(8)) and ((((A_i(7) and B_u(7)) or ((A_i(7) or B_u(7)) and ((A_i(6) and B_u(6)) or ((A_i(6) or B_u(6)) and ((A_i(5) and B_u(5)) or ((A_i(5) or B_u(5)) and ((A_i(4) and B_u(4)) or ((A_i(4) or B_u(4)) and ((((A_i(3) and B_u(3)) or ((A_i(3) or B_u(3)) and ((A_i(2) and B_u(2)) or ((A_i(2) or B_u(2)) and ((A_i(1) and B_u(1)) or ((A_i(1) or B_u(1)) and ((A_i(0) and B_u(0)) or ((A_i(0) or B_u(0)) and (mode_i))))))))) and perm(0)) or (mode_i and (not perm(0)))))))))))) and perm(1)) or (mode_i and (not perm(1)))))))))))) and perm(0)) or (mode_i and (not perm(0)))))))))))) and perm(2)) or (mode_i and (not perm(2)));
C_cla(17) <= (A_i(16) and B_u(16)) or ((A_i(16) or B_u(16)) and ((((A_i(15) and B_u(15)) or ((A_i(15) or B_u(15)) and ((A_i(14) and B_u(14)) or ((A_i(14) or B_u(14)) and ((A_i(13) and B_u(13)) or ((A_i(13) or B_u(13)) and ((A_i(12) and B_u(12)) or ((A_i(12) or B_u(12)) and ((((A_i(11) and B_u(11)) or ((A_i(11) or B_u(11)) and ((A_i(10) and B_u(10)) or ((A_i(10) or B_u(10)) and ((A_i(9) and B_u(9)) or ((A_i(9) or B_u(9)) and ((A_i(8) and B_u(8)) or ((A_i(8) or B_u(8)) and ((((A_i(7) and B_u(7)) or ((A_i(7) or B_u(7)) and ((A_i(6) and B_u(6)) or ((A_i(6) or B_u(6)) and ((A_i(5) and B_u(5)) or ((A_i(5) or B_u(5)) and ((A_i(4) and B_u(4)) or ((A_i(4) or B_u(4)) and ((((A_i(3) and B_u(3)) or ((A_i(3) or B_u(3)) and ((A_i(2) and B_u(2)) or ((A_i(2) or B_u(2)) and ((A_i(1) and B_u(1)) or ((A_i(1) or B_u(1)) and ((A_i(0) and B_u(0)) or ((A_i(0) or B_u(0)) and (mode_i))))))))) and perm(0)) or (mode_i and (not perm(0)))))))))))) and perm(1)) or (mode_i and (not perm(1)))))))))))) and perm(0)) or (mode_i and (not perm(0)))))))))))) and perm(2)) or (mode_i and (not perm(2)))));
C_cla(18) <= (A_i(17) and B_u(17)) or ((A_i(17) or B_u(17)) and ((A_i(16) and B_u(16)) or ((A_i(16) or B_u(16)) and ((((A_i(15) and B_u(15)) or ((A_i(15) or B_u(15)) and ((A_i(14) and B_u(14)) or ((A_i(14) or B_u(14)) and ((A_i(13) and B_u(13)) or ((A_i(13) or B_u(13)) and ((A_i(12) and B_u(12)) or ((A_i(12) or B_u(12)) and ((((A_i(11) and B_u(11)) or ((A_i(11) or B_u(11)) and ((A_i(10) and B_u(10)) or ((A_i(10) or B_u(10)) and ((A_i(9) and B_u(9)) or ((A_i(9) or B_u(9)) and ((A_i(8) and B_u(8)) or ((A_i(8) or B_u(8)) and ((((A_i(7) and B_u(7)) or ((A_i(7) or B_u(7)) and ((A_i(6) and B_u(6)) or ((A_i(6) or B_u(6)) and ((A_i(5) and B_u(5)) or ((A_i(5) or B_u(5)) and ((A_i(4) and B_u(4)) or ((A_i(4) or B_u(4)) and ((((A_i(3) and B_u(3)) or ((A_i(3) or B_u(3)) and ((A_i(2) and B_u(2)) or ((A_i(2) or B_u(2)) and ((A_i(1) and B_u(1)) or ((A_i(1) or B_u(1)) and ((A_i(0) and B_u(0)) or ((A_i(0) or B_u(0)) and (mode_i))))))))) and perm(0)) or (mode_i and (not perm(0)))))))))))) and perm(1)) or (mode_i and (not perm(1)))))))))))) and perm(0)) or (mode_i and (not perm(0)))))))))))) and perm(2)) or (mode_i and (not perm(2)))))));
C_cla(19) <= (A_i(18) and B_u(18)) or ((A_i(18) or B_u(18)) and ((A_i(17) and B_u(17)) or ((A_i(17) or B_u(17)) and ((A_i(16) and B_u(16)) or ((A_i(16) or B_u(16)) and ((((A_i(15) and B_u(15)) or ((A_i(15) or B_u(15)) and ((A_i(14) and B_u(14)) or ((A_i(14) or B_u(14)) and ((A_i(13) and B_u(13)) or ((A_i(13) or B_u(13)) and ((A_i(12) and B_u(12)) or ((A_i(12) or B_u(12)) and ((((A_i(11) and B_u(11)) or ((A_i(11) or B_u(11)) and ((A_i(10) and B_u(10)) or ((A_i(10) or B_u(10)) and ((A_i(9) and B_u(9)) or ((A_i(9) or B_u(9)) and ((A_i(8) and B_u(8)) or ((A_i(8) or B_u(8)) and ((((A_i(7) and B_u(7)) or ((A_i(7) or B_u(7)) and ((A_i(6) and B_u(6)) or ((A_i(6) or B_u(6)) and ((A_i(5) and B_u(5)) or ((A_i(5) or B_u(5)) and ((A_i(4) and B_u(4)) or ((A_i(4) or B_u(4)) and ((((A_i(3) and B_u(3)) or ((A_i(3) or B_u(3)) and ((A_i(2) and B_u(2)) or ((A_i(2) or B_u(2)) and ((A_i(1) and B_u(1)) or ((A_i(1) or B_u(1)) and ((A_i(0) and B_u(0)) or ((A_i(0) or B_u(0)) and (mode_i))))))))) and perm(0)) or (mode_i and (not perm(0)))))))))))) and perm(1)) or (mode_i and (not perm(1)))))))))))) and perm(0)) or (mode_i and (not perm(0)))))))))))) and perm(2)) or (mode_i and (not perm(2)))))))));
-- Subcampo 5 de 4 bits
C_cla(20) <= (((A_i(19) and B_u(19)) or ((A_i(19) or B_u(19)) and ((A_i(18) and B_u(18)) or ((A_i(18) or B_u(18)) and ((A_i(17) and B_u(17)) or ((A_i(17) or B_u(17)) and ((A_i(16) and B_u(16)) or ((A_i(16) or B_u(16)) and ((((A_i(15) and B_u(15)) or ((A_i(15) or B_u(15)) and ((A_i(14) and B_u(14)) or ((A_i(14) or B_u(14)) and ((A_i(13) and B_u(13)) or ((A_i(13) or B_u(13)) and ((A_i(12) and B_u(12)) or ((A_i(12) or B_u(12)) and ((((A_i(11) and B_u(11)) or ((A_i(11) or B_u(11)) and ((A_i(10) and B_u(10)) or ((A_i(10) or B_u(10)) and ((A_i(9) and B_u(9)) or ((A_i(9) or B_u(9)) and ((A_i(8) and B_u(8)) or ((A_i(8) or B_u(8)) and ((((A_i(7) and B_u(7)) or ((A_i(7) or B_u(7)) and ((A_i(6) and B_u(6)) or ((A_i(6) or B_u(6)) and ((A_i(5) and B_u(5)) or ((A_i(5) or B_u(5)) and ((A_i(4) and B_u(4)) or ((A_i(4) or B_u(4)) and ((((A_i(3) and B_u(3)) or ((A_i(3) or B_u(3)) and ((A_i(2) and B_u(2)) or ((A_i(2) or B_u(2)) and ((A_i(1) and B_u(1)) or ((A_i(1) or B_u(1)) and ((A_i(0) and B_u(0)) or ((A_i(0) or B_u(0)) and (mode_i))))))))) and perm(0)) or (mode_i and (not perm(0)))))))))))) and perm(1)) or (mode_i and (not perm(1)))))))))))) and perm(0)) or (mode_i and (not perm(0)))))))))))) and perm(2)) or (mode_i and (not perm(2)))))))))))) and perm(0)) or (mode_i and (not perm(0)));
C_cla(21) <= (A_i(20) and B_u(20)) or ((A_i(20) or B_u(20)) and ((((A_i(19) and B_u(19)) or ((A_i(19) or B_u(19)) and ((A_i(18) and B_u(18)) or ((A_i(18) or B_u(18)) and ((A_i(17) and B_u(17)) or ((A_i(17) or B_u(17)) and ((A_i(16) and B_u(16)) or ((A_i(16) or B_u(16)) and ((((A_i(15) and B_u(15)) or ((A_i(15) or B_u(15)) and ((A_i(14) and B_u(14)) or ((A_i(14) or B_u(14)) and ((A_i(13) and B_u(13)) or ((A_i(13) or B_u(13)) and ((A_i(12) and B_u(12)) or ((A_i(12) or B_u(12)) and ((((A_i(11) and B_u(11)) or ((A_i(11) or B_u(11)) and ((A_i(10) and B_u(10)) or ((A_i(10) or B_u(10)) and ((A_i(9) and B_u(9)) or ((A_i(9) or B_u(9)) and ((A_i(8) and B_u(8)) or ((A_i(8) or B_u(8)) and ((((A_i(7) and B_u(7)) or ((A_i(7) or B_u(7)) and ((A_i(6) and B_u(6)) or ((A_i(6) or B_u(6)) and ((A_i(5) and B_u(5)) or ((A_i(5) or B_u(5)) and ((A_i(4) and B_u(4)) or ((A_i(4) or B_u(4)) and ((((A_i(3) and B_u(3)) or ((A_i(3) or B_u(3)) and ((A_i(2) and B_u(2)) or ((A_i(2) or B_u(2)) and ((A_i(1) and B_u(1)) or ((A_i(1) or B_u(1)) and ((A_i(0) and B_u(0)) or ((A_i(0) or B_u(0)) and (mode_i))))))))) and perm(0)) or (mode_i and (not perm(0)))))))))))) and perm(1)) or (mode_i and (not perm(1)))))))))))) and perm(0)) or (mode_i and (not perm(0)))))))))))) and perm(2)) or (mode_i and (not perm(2)))))))))))) and perm(0)) or (mode_i and (not perm(0)))));
C_cla(22) <= (A_i(21) and B_u(21)) or ((A_i(21) or B_u(21)) and ((A_i(20) and B_u(20)) or ((A_i(20) or B_u(20)) and ((((A_i(19) and B_u(19)) or ((A_i(19) or B_u(19)) and ((A_i(18) and B_u(18)) or ((A_i(18) or B_u(18)) and ((A_i(17) and B_u(17)) or ((A_i(17) or B_u(17)) and ((A_i(16) and B_u(16)) or ((A_i(16) or B_u(16)) and ((((A_i(15) and B_u(15)) or ((A_i(15) or B_u(15)) and ((A_i(14) and B_u(14)) or ((A_i(14) or B_u(14)) and ((A_i(13) and B_u(13)) or ((A_i(13) or B_u(13)) and ((A_i(12) and B_u(12)) or ((A_i(12) or B_u(12)) and ((((A_i(11) and B_u(11)) or ((A_i(11) or B_u(11)) and ((A_i(10) and B_u(10)) or ((A_i(10) or B_u(10)) and ((A_i(9) and B_u(9)) or ((A_i(9) or B_u(9)) and ((A_i(8) and B_u(8)) or ((A_i(8) or B_u(8)) and ((((A_i(7) and B_u(7)) or ((A_i(7) or B_u(7)) and ((A_i(6) and B_u(6)) or ((A_i(6) or B_u(6)) and ((A_i(5) and B_u(5)) or ((A_i(5) or B_u(5)) and ((A_i(4) and B_u(4)) or ((A_i(4) or B_u(4)) and ((((A_i(3) and B_u(3)) or ((A_i(3) or B_u(3)) and ((A_i(2) and B_u(2)) or ((A_i(2) or B_u(2)) and ((A_i(1) and B_u(1)) or ((A_i(1) or B_u(1)) and ((A_i(0) and B_u(0)) or ((A_i(0) or B_u(0)) and (mode_i))))))))) and perm(0)) or (mode_i and (not perm(0)))))))))))) and perm(1)) or (mode_i and (not perm(1)))))))))))) and perm(0)) or (mode_i and (not perm(0)))))))))))) and perm(2)) or (mode_i and (not perm(2)))))))))))) and perm(0)) or (mode_i and (not perm(0)))))));
C_cla(23) <= (A_i(22) and B_u(22)) or ((A_i(22) or B_u(22)) and ((A_i(21) and B_u(21)) or ((A_i(21) or B_u(21)) and ((A_i(20) and B_u(20)) or ((A_i(20) or B_u(20)) and ((((A_i(19) and B_u(19)) or ((A_i(19) or B_u(19)) and ((A_i(18) and B_u(18)) or ((A_i(18) or B_u(18)) and ((A_i(17) and B_u(17)) or ((A_i(17) or B_u(17)) and ((A_i(16) and B_u(16)) or ((A_i(16) or B_u(16)) and ((((A_i(15) and B_u(15)) or ((A_i(15) or B_u(15)) and ((A_i(14) and B_u(14)) or ((A_i(14) or B_u(14)) and ((A_i(13) and B_u(13)) or ((A_i(13) or B_u(13)) and ((A_i(12) and B_u(12)) or ((A_i(12) or B_u(12)) and ((((A_i(11) and B_u(11)) or ((A_i(11) or B_u(11)) and ((A_i(10) and B_u(10)) or ((A_i(10) or B_u(10)) and ((A_i(9) and B_u(9)) or ((A_i(9) or B_u(9)) and ((A_i(8) and B_u(8)) or ((A_i(8) or B_u(8)) and ((((A_i(7) and B_u(7)) or ((A_i(7) or B_u(7)) and ((A_i(6) and B_u(6)) or ((A_i(6) or B_u(6)) and ((A_i(5) and B_u(5)) or ((A_i(5) or B_u(5)) and ((A_i(4) and B_u(4)) or ((A_i(4) or B_u(4)) and ((((A_i(3) and B_u(3)) or ((A_i(3) or B_u(3)) and ((A_i(2) and B_u(2)) or ((A_i(2) or B_u(2)) and ((A_i(1) and B_u(1)) or ((A_i(1) or B_u(1)) and ((A_i(0) and B_u(0)) or ((A_i(0) or B_u(0)) and (mode_i))))))))) and perm(0)) or (mode_i and (not perm(0)))))))))))) and perm(1)) or (mode_i and (not perm(1)))))))))))) and perm(0)) or (mode_i and (not perm(0)))))))))))) and perm(2)) or (mode_i and (not perm(2)))))))))))) and perm(0)) or (mode_i and (not perm(0)))))))));
-- Subcampo 6 de 4 bits
C_cla(24) <= (((A_i(23) and B_u(23)) or ((A_i(23) or B_u(23)) and ((A_i(22) and B_u(22)) or ((A_i(22) or B_u(22)) and ((A_i(21) and B_u(21)) or ((A_i(21) or B_u(21)) and ((A_i(20) and B_u(20)) or ((A_i(20) or B_u(20)) and ((((A_i(19) and B_u(19)) or ((A_i(19) or B_u(19)) and ((A_i(18) and B_u(18)) or ((A_i(18) or B_u(18)) and ((A_i(17) and B_u(17)) or ((A_i(17) or B_u(17)) and ((A_i(16) and B_u(16)) or ((A_i(16) or B_u(16)) and ((((A_i(15) and B_u(15)) or ((A_i(15) or B_u(15)) and ((A_i(14) and B_u(14)) or ((A_i(14) or B_u(14)) and ((A_i(13) and B_u(13)) or ((A_i(13) or B_u(13)) and ((A_i(12) and B_u(12)) or ((A_i(12) or B_u(12)) and ((((A_i(11) and B_u(11)) or ((A_i(11) or B_u(11)) and ((A_i(10) and B_u(10)) or ((A_i(10) or B_u(10)) and ((A_i(9) and B_u(9)) or ((A_i(9) or B_u(9)) and ((A_i(8) and B_u(8)) or ((A_i(8) or B_u(8)) and ((((A_i(7) and B_u(7)) or ((A_i(7) or B_u(7)) and ((A_i(6) and B_u(6)) or ((A_i(6) or B_u(6)) and ((A_i(5) and B_u(5)) or ((A_i(5) or B_u(5)) and ((A_i(4) and B_u(4)) or ((A_i(4) or B_u(4)) and ((((A_i(3) and B_u(3)) or ((A_i(3) or B_u(3)) and ((A_i(2) and B_u(2)) or ((A_i(2) or B_u(2)) and ((A_i(1) and B_u(1)) or ((A_i(1) or B_u(1)) and ((A_i(0) and B_u(0)) or ((A_i(0) or B_u(0)) and (mode_i))))))))) and perm(0)) or (mode_i and (not perm(0)))))))))))) and perm(1)) or (mode_i and (not perm(1)))))))))))) and perm(0)) or (mode_i and (not perm(0)))))))))))) and perm(2)) or (mode_i and (not perm(2)))))))))))) and perm(0)) or (mode_i and (not perm(0)))))))))))) and perm(1)) or (mode_i and (not perm(1)));
C_cla(25) <= (A_i(24) and B_u(24)) or ((A_i(24) or B_u(24)) and ((((A_i(23) and B_u(23)) or ((A_i(23) or B_u(23)) and ((A_i(22) and B_u(22)) or ((A_i(22) or B_u(22)) and ((A_i(21) and B_u(21)) or ((A_i(21) or B_u(21)) and ((A_i(20) and B_u(20)) or ((A_i(20) or B_u(20)) and ((((A_i(19) and B_u(19)) or ((A_i(19) or B_u(19)) and ((A_i(18) and B_u(18)) or ((A_i(18) or B_u(18)) and ((A_i(17) and B_u(17)) or ((A_i(17) or B_u(17)) and ((A_i(16) and B_u(16)) or ((A_i(16) or B_u(16)) and ((((A_i(15) and B_u(15)) or ((A_i(15) or B_u(15)) and ((A_i(14) and B_u(14)) or ((A_i(14) or B_u(14)) and ((A_i(13) and B_u(13)) or ((A_i(13) or B_u(13)) and ((A_i(12) and B_u(12)) or ((A_i(12) or B_u(12)) and ((((A_i(11) and B_u(11)) or ((A_i(11) or B_u(11)) and ((A_i(10) and B_u(10)) or ((A_i(10) or B_u(10)) and ((A_i(9) and B_u(9)) or ((A_i(9) or B_u(9)) and ((A_i(8) and B_u(8)) or ((A_i(8) or B_u(8)) and ((((A_i(7) and B_u(7)) or ((A_i(7) or B_u(7)) and ((A_i(6) and B_u(6)) or ((A_i(6) or B_u(6)) and ((A_i(5) and B_u(5)) or ((A_i(5) or B_u(5)) and ((A_i(4) and B_u(4)) or ((A_i(4) or B_u(4)) and ((((A_i(3) and B_u(3)) or ((A_i(3) or B_u(3)) and ((A_i(2) and B_u(2)) or ((A_i(2) or B_u(2)) and ((A_i(1) and B_u(1)) or ((A_i(1) or B_u(1)) and ((A_i(0) and B_u(0)) or ((A_i(0) or B_u(0)) and (mode_i))))))))) and perm(0)) or (mode_i and (not perm(0)))))))))))) and perm(1)) or (mode_i and (not perm(1)))))))))))) and perm(0)) or (mode_i and (not perm(0)))))))))))) and perm(2)) or (mode_i and (not perm(2)))))))))))) and perm(0)) or (mode_i and (not perm(0)))))))))))) and perm(1)) or (mode_i and (not perm(1)))));
C_cla(26) <= (A_i(25) and B_u(25)) or ((A_i(25) or B_u(25)) and ((A_i(24) and B_u(24)) or ((A_i(24) or B_u(24)) and ((((A_i(23) and B_u(23)) or ((A_i(23) or B_u(23)) and ((A_i(22) and B_u(22)) or ((A_i(22) or B_u(22)) and ((A_i(21) and B_u(21)) or ((A_i(21) or B_u(21)) and ((A_i(20) and B_u(20)) or ((A_i(20) or B_u(20)) and ((((A_i(19) and B_u(19)) or ((A_i(19) or B_u(19)) and ((A_i(18) and B_u(18)) or ((A_i(18) or B_u(18)) and ((A_i(17) and B_u(17)) or ((A_i(17) or B_u(17)) and ((A_i(16) and B_u(16)) or ((A_i(16) or B_u(16)) and ((((A_i(15) and B_u(15)) or ((A_i(15) or B_u(15)) and ((A_i(14) and B_u(14)) or ((A_i(14) or B_u(14)) and ((A_i(13) and B_u(13)) or ((A_i(13) or B_u(13)) and ((A_i(12) and B_u(12)) or ((A_i(12) or B_u(12)) and ((((A_i(11) and B_u(11)) or ((A_i(11) or B_u(11)) and ((A_i(10) and B_u(10)) or ((A_i(10) or B_u(10)) and ((A_i(9) and B_u(9)) or ((A_i(9) or B_u(9)) and ((A_i(8) and B_u(8)) or ((A_i(8) or B_u(8)) and ((((A_i(7) and B_u(7)) or ((A_i(7) or B_u(7)) and ((A_i(6) and B_u(6)) or ((A_i(6) or B_u(6)) and ((A_i(5) and B_u(5)) or ((A_i(5) or B_u(5)) and ((A_i(4) and B_u(4)) or ((A_i(4) or B_u(4)) and ((((A_i(3) and B_u(3)) or ((A_i(3) or B_u(3)) and ((A_i(2) and B_u(2)) or ((A_i(2) or B_u(2)) and ((A_i(1) and B_u(1)) or ((A_i(1) or B_u(1)) and ((A_i(0) and B_u(0)) or ((A_i(0) or B_u(0)) and (mode_i))))))))) and perm(0)) or (mode_i and (not perm(0)))))))))))) and perm(1)) or (mode_i and (not perm(1)))))))))))) and perm(0)) or (mode_i and (not perm(0)))))))))))) and perm(2)) or (mode_i and (not perm(2)))))))))))) and perm(0)) or (mode_i and (not perm(0)))))))))))) and perm(1)) or (mode_i and (not perm(1)))))));
C_cla(27) <= (A_i(26) and B_u(26)) or ((A_i(26) or B_u(26)) and ((A_i(25) and B_u(25)) or ((A_i(25) or B_u(25)) and ((A_i(24) and B_u(24)) or ((A_i(24) or B_u(24)) and ((((A_i(23) and B_u(23)) or ((A_i(23) or B_u(23)) and ((A_i(22) and B_u(22)) or ((A_i(22) or B_u(22)) and ((A_i(21) and B_u(21)) or ((A_i(21) or B_u(21)) and ((A_i(20) and B_u(20)) or ((A_i(20) or B_u(20)) and ((((A_i(19) and B_u(19)) or ((A_i(19) or B_u(19)) and ((A_i(18) and B_u(18)) or ((A_i(18) or B_u(18)) and ((A_i(17) and B_u(17)) or ((A_i(17) or B_u(17)) and ((A_i(16) and B_u(16)) or ((A_i(16) or B_u(16)) and ((((A_i(15) and B_u(15)) or ((A_i(15) or B_u(15)) and ((A_i(14) and B_u(14)) or ((A_i(14) or B_u(14)) and ((A_i(13) and B_u(13)) or ((A_i(13) or B_u(13)) and ((A_i(12) and B_u(12)) or ((A_i(12) or B_u(12)) and ((((A_i(11) and B_u(11)) or ((A_i(11) or B_u(11)) and ((A_i(10) and B_u(10)) or ((A_i(10) or B_u(10)) and ((A_i(9) and B_u(9)) or ((A_i(9) or B_u(9)) and ((A_i(8) and B_u(8)) or ((A_i(8) or B_u(8)) and ((((A_i(7) and B_u(7)) or ((A_i(7) or B_u(7)) and ((A_i(6) and B_u(6)) or ((A_i(6) or B_u(6)) and ((A_i(5) and B_u(5)) or ((A_i(5) or B_u(5)) and ((A_i(4) and B_u(4)) or ((A_i(4) or B_u(4)) and ((((A_i(3) and B_u(3)) or ((A_i(3) or B_u(3)) and ((A_i(2) and B_u(2)) or ((A_i(2) or B_u(2)) and ((A_i(1) and B_u(1)) or ((A_i(1) or B_u(1)) and ((A_i(0) and B_u(0)) or ((A_i(0) or B_u(0)) and (mode_i))))))))) and perm(0)) or (mode_i and (not perm(0)))))))))))) and perm(1)) or (mode_i and (not perm(1)))))))))))) and perm(0)) or (mode_i and (not perm(0)))))))))))) and perm(2)) or (mode_i and (not perm(2)))))))))))) and perm(0)) or (mode_i and (not perm(0)))))))))))) and perm(1)) or (mode_i and (not perm(1)))))))));
-- Subcampo 7 de 4 bits
C_cla(28) <= (((A_i(27) and B_u(27)) or ((A_i(27) or B_u(27)) and ((A_i(26) and B_u(26)) or ((A_i(26) or B_u(26)) and ((A_i(25) and B_u(25)) or ((A_i(25) or B_u(25)) and ((A_i(24) and B_u(24)) or ((A_i(24) or B_u(24)) and ((((A_i(23) and B_u(23)) or ((A_i(23) or B_u(23)) and ((A_i(22) and B_u(22)) or ((A_i(22) or B_u(22)) and ((A_i(21) and B_u(21)) or ((A_i(21) or B_u(21)) and ((A_i(20) and B_u(20)) or ((A_i(20) or B_u(20)) and ((((A_i(19) and B_u(19)) or ((A_i(19) or B_u(19)) and ((A_i(18) and B_u(18)) or ((A_i(18) or B_u(18)) and ((A_i(17) and B_u(17)) or ((A_i(17) or B_u(17)) and ((A_i(16) and B_u(16)) or ((A_i(16) or B_u(16)) and ((((A_i(15) and B_u(15)) or ((A_i(15) or B_u(15)) and ((A_i(14) and B_u(14)) or ((A_i(14) or B_u(14)) and ((A_i(13) and B_u(13)) or ((A_i(13) or B_u(13)) and ((A_i(12) and B_u(12)) or ((A_i(12) or B_u(12)) and ((((A_i(11) and B_u(11)) or ((A_i(11) or B_u(11)) and ((A_i(10) and B_u(10)) or ((A_i(10) or B_u(10)) and ((A_i(9) and B_u(9)) or ((A_i(9) or B_u(9)) and ((A_i(8) and B_u(8)) or ((A_i(8) or B_u(8)) and ((((A_i(7) and B_u(7)) or ((A_i(7) or B_u(7)) and ((A_i(6) and B_u(6)) or ((A_i(6) or B_u(6)) and ((A_i(5) and B_u(5)) or ((A_i(5) or B_u(5)) and ((A_i(4) and B_u(4)) or ((A_i(4) or B_u(4)) and ((((A_i(3) and B_u(3)) or ((A_i(3) or B_u(3)) and ((A_i(2) and B_u(2)) or ((A_i(2) or B_u(2)) and ((A_i(1) and B_u(1)) or ((A_i(1) or B_u(1)) and ((A_i(0) and B_u(0)) or ((A_i(0) or B_u(0)) and (mode_i))))))))) and perm(0)) or (mode_i and (not perm(0)))))))))))) and perm(1)) or (mode_i and (not perm(1)))))))))))) and perm(0)) or (mode_i and (not perm(0)))))))))))) and perm(2)) or (mode_i and (not perm(2)))))))))))) and perm(0)) or (mode_i and (not perm(0)))))))))))) and perm(1)) or (mode_i and (not perm(1)))))))))))) and perm(0)) or (mode_i and (not perm(0)));
C_cla(29) <= (A_i(28) and B_u(28)) or ((A_i(28) or B_u(28)) and ((((A_i(27) and B_u(27)) or ((A_i(27) or B_u(27)) and ((A_i(26) and B_u(26)) or ((A_i(26) or B_u(26)) and ((A_i(25) and B_u(25)) or ((A_i(25) or B_u(25)) and ((A_i(24) and B_u(24)) or ((A_i(24) or B_u(24)) and ((((A_i(23) and B_u(23)) or ((A_i(23) or B_u(23)) and ((A_i(22) and B_u(22)) or ((A_i(22) or B_u(22)) and ((A_i(21) and B_u(21)) or ((A_i(21) or B_u(21)) and ((A_i(20) and B_u(20)) or ((A_i(20) or B_u(20)) and ((((A_i(19) and B_u(19)) or ((A_i(19) or B_u(19)) and ((A_i(18) and B_u(18)) or ((A_i(18) or B_u(18)) and ((A_i(17) and B_u(17)) or ((A_i(17) or B_u(17)) and ((A_i(16) and B_u(16)) or ((A_i(16) or B_u(16)) and ((((A_i(15) and B_u(15)) or ((A_i(15) or B_u(15)) and ((A_i(14) and B_u(14)) or ((A_i(14) or B_u(14)) and ((A_i(13) and B_u(13)) or ((A_i(13) or B_u(13)) and ((A_i(12) and B_u(12)) or ((A_i(12) or B_u(12)) and ((((A_i(11) and B_u(11)) or ((A_i(11) or B_u(11)) and ((A_i(10) and B_u(10)) or ((A_i(10) or B_u(10)) and ((A_i(9) and B_u(9)) or ((A_i(9) or B_u(9)) and ((A_i(8) and B_u(8)) or ((A_i(8) or B_u(8)) and ((((A_i(7) and B_u(7)) or ((A_i(7) or B_u(7)) and ((A_i(6) and B_u(6)) or ((A_i(6) or B_u(6)) and ((A_i(5) and B_u(5)) or ((A_i(5) or B_u(5)) and ((A_i(4) and B_u(4)) or ((A_i(4) or B_u(4)) and ((((A_i(3) and B_u(3)) or ((A_i(3) or B_u(3)) and ((A_i(2) and B_u(2)) or ((A_i(2) or B_u(2)) and ((A_i(1) and B_u(1)) or ((A_i(1) or B_u(1)) and ((A_i(0) and B_u(0)) or ((A_i(0) or B_u(0)) and (mode_i))))))))) and perm(0)) or (mode_i and (not perm(0)))))))))))) and perm(1)) or (mode_i and (not perm(1)))))))))))) and perm(0)) or (mode_i and (not perm(0)))))))))))) and perm(2)) or (mode_i and (not perm(2)))))))))))) and perm(0)) or (mode_i and (not perm(0)))))))))))) and perm(1)) or (mode_i and (not perm(1)))))))))))) and perm(0)) or (mode_i and (not perm(0)))));
C_cla(30) <= (A_i(29) and B_u(29)) or ((A_i(29) or B_u(29)) and ((A_i(28) and B_u(28)) or ((A_i(28) or B_u(28)) and ((((A_i(27) and B_u(27)) or ((A_i(27) or B_u(27)) and ((A_i(26) and B_u(26)) or ((A_i(26) or B_u(26)) and ((A_i(25) and B_u(25)) or ((A_i(25) or B_u(25)) and ((A_i(24) and B_u(24)) or ((A_i(24) or B_u(24)) and ((((A_i(23) and B_u(23)) or ((A_i(23) or B_u(23)) and ((A_i(22) and B_u(22)) or ((A_i(22) or B_u(22)) and ((A_i(21) and B_u(21)) or ((A_i(21) or B_u(21)) and ((A_i(20) and B_u(20)) or ((A_i(20) or B_u(20)) and ((((A_i(19) and B_u(19)) or ((A_i(19) or B_u(19)) and ((A_i(18) and B_u(18)) or ((A_i(18) or B_u(18)) and ((A_i(17) and B_u(17)) or ((A_i(17) or B_u(17)) and ((A_i(16) and B_u(16)) or ((A_i(16) or B_u(16)) and ((((A_i(15) and B_u(15)) or ((A_i(15) or B_u(15)) and ((A_i(14) and B_u(14)) or ((A_i(14) or B_u(14)) and ((A_i(13) and B_u(13)) or ((A_i(13) or B_u(13)) and ((A_i(12) and B_u(12)) or ((A_i(12) or B_u(12)) and ((((A_i(11) and B_u(11)) or ((A_i(11) or B_u(11)) and ((A_i(10) and B_u(10)) or ((A_i(10) or B_u(10)) and ((A_i(9) and B_u(9)) or ((A_i(9) or B_u(9)) and ((A_i(8) and B_u(8)) or ((A_i(8) or B_u(8)) and ((((A_i(7) and B_u(7)) or ((A_i(7) or B_u(7)) and ((A_i(6) and B_u(6)) or ((A_i(6) or B_u(6)) and ((A_i(5) and B_u(5)) or ((A_i(5) or B_u(5)) and ((A_i(4) and B_u(4)) or ((A_i(4) or B_u(4)) and ((((A_i(3) and B_u(3)) or ((A_i(3) or B_u(3)) and ((A_i(2) and B_u(2)) or ((A_i(2) or B_u(2)) and ((A_i(1) and B_u(1)) or ((A_i(1) or B_u(1)) and ((A_i(0) and B_u(0)) or ((A_i(0) or B_u(0)) and (mode_i))))))))) and perm(0)) or (mode_i and (not perm(0)))))))))))) and perm(1)) or (mode_i and (not perm(1)))))))))))) and perm(0)) or (mode_i and (not perm(0)))))))))))) and perm(2)) or (mode_i and (not perm(2)))))))))))) and perm(0)) or (mode_i and (not perm(0)))))))))))) and perm(1)) or (mode_i and (not perm(1)))))))))))) and perm(0)) or (mode_i and (not perm(0)))))));
C_cla(31) <= (A_i(30) and B_u(30)) or ((A_i(30) or B_u(30)) and ((A_i(29) and B_u(29)) or ((A_i(29) or B_u(29)) and ((A_i(28) and B_u(28)) or ((A_i(28) or B_u(28)) and ((((A_i(27) and B_u(27)) or ((A_i(27) or B_u(27)) and ((A_i(26) and B_u(26)) or ((A_i(26) or B_u(26)) and ((A_i(25) and B_u(25)) or ((A_i(25) or B_u(25)) and ((A_i(24) and B_u(24)) or ((A_i(24) or B_u(24)) and ((((A_i(23) and B_u(23)) or ((A_i(23) or B_u(23)) and ((A_i(22) and B_u(22)) or ((A_i(22) or B_u(22)) and ((A_i(21) and B_u(21)) or ((A_i(21) or B_u(21)) and ((A_i(20) and B_u(20)) or ((A_i(20) or B_u(20)) and ((((A_i(19) and B_u(19)) or ((A_i(19) or B_u(19)) and ((A_i(18) and B_u(18)) or ((A_i(18) or B_u(18)) and ((A_i(17) and B_u(17)) or ((A_i(17) or B_u(17)) and ((A_i(16) and B_u(16)) or ((A_i(16) or B_u(16)) and ((((A_i(15) and B_u(15)) or ((A_i(15) or B_u(15)) and ((A_i(14) and B_u(14)) or ((A_i(14) or B_u(14)) and ((A_i(13) and B_u(13)) or ((A_i(13) or B_u(13)) and ((A_i(12) and B_u(12)) or ((A_i(12) or B_u(12)) and ((((A_i(11) and B_u(11)) or ((A_i(11) or B_u(11)) and ((A_i(10) and B_u(10)) or ((A_i(10) or B_u(10)) and ((A_i(9) and B_u(9)) or ((A_i(9) or B_u(9)) and ((A_i(8) and B_u(8)) or ((A_i(8) or B_u(8)) and ((((A_i(7) and B_u(7)) or ((A_i(7) or B_u(7)) and ((A_i(6) and B_u(6)) or ((A_i(6) or B_u(6)) and ((A_i(5) and B_u(5)) or ((A_i(5) or B_u(5)) and ((A_i(4) and B_u(4)) or ((A_i(4) or B_u(4)) and ((((A_i(3) and B_u(3)) or ((A_i(3) or B_u(3)) and ((A_i(2) and B_u(2)) or ((A_i(2) or B_u(2)) and ((A_i(1) and B_u(1)) or ((A_i(1) or B_u(1)) and ((A_i(0) and B_u(0)) or ((A_i(0) or B_u(0)) and (mode_i))))))))) and perm(0)) or (mode_i and (not perm(0)))))))))))) and perm(1)) or (mode_i and (not perm(1)))))))))))) and perm(0)) or (mode_i and (not perm(0)))))))))))) and perm(2)) or (mode_i and (not perm(2)))))))))))) and perm(0)) or (mode_i and (not perm(0)))))))))))) and perm(1)) or (mode_i and (not perm(1)))))))))))) and perm(0)) or (mode_i and (not perm(0)))))))));




-- Realizar a soma
-- Subcampo 0 de 4 bits
S_i(0) <= (A_i(0) xor B_u(0)) xor C_cla(0);
S_i(1) <= (A_i(1) xor B_u(1)) xor C_cla(1);
S_i(2) <= (A_i(2) xor B_u(2)) xor C_cla(2);
S_i(3) <= (A_i(3) xor B_u(3)) xor C_cla(3);
-- Subcampo 1 de 4 bits
S_i(4) <= (A_i(4) xor B_u(4)) xor C_cla(4);
S_i(5) <= (A_i(5) xor B_u(5)) xor C_cla(5);
S_i(6) <= (A_i(6) xor B_u(6)) xor C_cla(6);
S_i(7) <= (A_i(7) xor B_u(7)) xor C_cla(7);
-- Subcampo 2 de 4 bits
S_i(8) <= (A_i(8) xor B_u(8)) xor C_cla(8);
S_i(9) <= (A_i(9) xor B_u(9)) xor C_cla(9);
S_i(10) <= (A_i(10) xor B_u(10)) xor C_cla(10);
S_i(11) <= (A_i(11) xor B_u(11)) xor C_cla(11);
-- Subcampo 3 de 4 bits
S_i(12) <= (A_i(12) xor B_u(12)) xor C_cla(12);
S_i(13) <= (A_i(13) xor B_u(13)) xor C_cla(13);
S_i(14) <= (A_i(14) xor B_u(14)) xor C_cla(14);
S_i(15) <= (A_i(15) xor B_u(15)) xor C_cla(15);
-- Subcampo 4 de 4 bit
S_i(16) <= (A_i(16) xor B_u(16)) xor C_cla(16);
S_i(17) <= (A_i(17) xor B_u(17)) xor C_cla(17);
S_i(18) <= (A_i(18) xor B_u(18)) xor C_cla(18);
S_i(19) <= (A_i(19) xor B_u(19)) xor C_cla(19);
-- Subcampo 5 de 4 bits
S_i(20) <= (A_i(20) xor B_u(20)) xor C_cla(20);
S_i(21) <= (A_i(21) xor B_u(21)) xor C_cla(21);
S_i(22) <= (A_i(22) xor B_u(22)) xor C_cla(22);
S_i(23) <= (A_i(23) xor B_u(23)) xor C_cla(23);
-- Subcampo 6 de 4 bits
S_i(24) <= (A_i(24) xor B_u(24)) xor C_cla(24);
S_i(25) <= (A_i(25) xor B_u(25)) xor C_cla(25);
S_i(26) <= (A_i(26) xor B_u(26)) xor C_cla(26);
S_i(27) <= (A_i(27) xor B_u(27)) xor C_cla(27);
-- Subcampo 7 de 4 bits
S_i(28) <= (A_i(28) xor B_u(28)) xor C_cla(28);
S_i(29) <= (A_i(29) xor B_u(29)) xor C_cla(29);
S_i(30) <= (A_i(30) xor B_u(30)) xor C_cla(30);
S_i(31) <= (A_i(31) xor B_u(31)) xor C_cla(31);

-- Sexto passo: otimizar isso com nands
-- Sétimo passo: vitória

END TypeArchitecture;
